// Logisim project VS80.circ as structural Verilog: 7 circuits, main circuit control
module main (
);

  wire CLK, clock_1_out, REG_A_OUT, REG_A_WRITE, REG_B_OUT, REG_B_WRITE, REGISTER_CLEAR;
  wire [2:0] CLK_BUS;
  wire [3:0] CTR_CTRL;
  wire [7:0] DBUS;

  Clock clock_1 (.out(clock_1_out));
  control CONTROL_MODULE (
    .CLK_IN(CLK), .DBUS(DBUS), .CLK_PLS(CLK_BUS[0]), .CLK_EN(CLK_BUS[1]), .CLK_HALT(CLK_BUS[2]),
    .CTR_EN(CTR_CTRL[0]), .CTR_CLR(CTR_CTRL[1]), .CTR_JMP(CTR_CTRL[2]), .CTR_OUT(CTR_CTRL[3]),
    .REGA_OUTPUT(REG_A_OUT), .REGA_WRITE(REG_A_WRITE), .REGB_OUTPUT(REG_B_OUT), .REGB_WRITE(REG_B_WRITE),
    .REGISTER_CLEAR(REGISTER_CLEAR));
  clock_module clock_module_1 (
    .IN_555(clock_1_out), .IN_PULSE(CLK_BUS[0]), .IN_CLOCK_EN(CLK_BUS[1]), .IN_HALT(CLK_BUS[2]), .CLK_OUT(CLK));
  program_counter program_counter_1 (
    .CTR_ENABLE(CTR_CTRL[0]), .CTR_CLEAR(CTR_CTRL[1]), .CTR_JMP(CTR_CTRL[2]), .COUNT_OUT(CTR_CTRL[3]),
    .CLK(CLK), .DBUS(DBUS));
  Pull_Resistor pull_resistor_1 (.node(DBUS));
  // LedBar #(.inputtype("row")) ledbar_1: pin names not known; wires that end beside it: DBUS
  gen_register gen_register_1 (
    .WRITE_ENABLE(REG_A_WRITE), .CLEAR(REGISTER_CLEAR), .CLK(CLK), .DBUS(DBUS));  // open: OUTPUT_ENABLE
  gen_register gen_register_2 (
    .WRITE_ENABLE(REG_B_WRITE), .OUTPUT_ENABLE(REG_B_OUT), .CLEAR(REGISTER_CLEAR), .CLK(CLK), .DBUS(DBUS));
endmodule

module clock_module (
  input  IN_555,
  input  IN_PULSE,
  input  IN_CLOCK_EN,
  input  IN_HALT,
  output CLK_OUT
);

  wire nor_1_out, nor_2_out, nor_3_out;

  nor nor_1 (nor_1_out, ~IN_555, ~IN_CLOCK_EN);  // NOR_Gate
  nor nor_2 (nor_2_out, ~IN_PULSE, IN_CLOCK_EN);  // NOR_Gate
  nor nor_3 (nor_3_out, nor_1_out, nor_2_out);
  nor nor_4 (CLK_OUT, nor_3_out, IN_HALT);

  // Notes on the sheet:
  //   IN_CLOCK_EN Describes whether or not we use the 555 astable signal, or the manual pulse control.
endmodule

module program_counter (
  input  CTR_ENABLE,
  input  CTR_CLEAR,
  input  CTR_JMP,
  input  COUNT_OUT,
  input  CLK,
  output [7:0] DBUS
);

  wire n74161_1_pin15;
  wire [7:0] n74161_1_pin14;

  Pull_Resistor pull_resistor_1 (.node(DBUS));
  _74161 u_74161_1 (
    .pin1(CTR_CLEAR), .pin2(CLK), .pin3(DBUS[0]), .pin4(DBUS[1]), .pin5(DBUS[2]), .pin6(DBUS[3]),
    .pin7(CTR_ENABLE), .pin15(n74161_1_pin15), .pin14(n74161_1_pin14[0]), .pin13(n74161_1_pin14[1]),
    .pin12(n74161_1_pin14[2]), .pin11(n74161_1_pin14[3]), .pin10(CTR_ENABLE), .pin9(CTR_JMP));
  assign DBUS = COUNT_OUT ? n74161_1_pin14 : 8'bz;  // Controlled_Buffer controlled_buffer_1
  _74161 u_74161_2 (
    .pin1(CTR_CLEAR), .pin2(CLK), .pin3(DBUS[4]), .pin4(DBUS[5]), .pin5(DBUS[6]), .pin6(DBUS[7]),
    .pin7(CTR_ENABLE), .pin14(n74161_1_pin14[4]), .pin13(n74161_1_pin14[5]), .pin12(n74161_1_pin14[6]),
    .pin11(n74161_1_pin14[7]), .pin10(n74161_1_pin15), .pin9(CTR_JMP));  // open: pin15
  // LedBar #(.inputtype("row")) ledbar_1: pin names not known; wires that end beside it: n74161_1_pin14

  // Notes on the sheet:
  //   jump/load line
  //   carry line
  //   output
  //   inputs
endmodule

module control (
  input  CLK_IN,
  output [7:0] DBUS,
  output CLK_PLS,
  output CLK_EN,
  output CLK_HALT,
  output CTR_EN,
  output CTR_CLR,
  output CTR_JMP,
  output CTR_OUT,
  output REGA_OUTPUT,
  output REGA_WRITE,
  output REGB_OUTPUT,
  output REGB_WRITE,
  output REGISTER_CLEAR
);

  wire pull_resistor_10_node, pull_resistor_14_node, switch_1_p1, switch_2_p1, switch_3_p1, switch_4_p1,
       switch_5_p1, switch_6_p1, switch_7_p1, switch_9_p1, switch_10_p1, switch_11_p1;
  wire [7:0] DATA_INPUT_sw1;

  Button button_1 (.out(CLK_PLS));
  Pull_Resistor pull_resistor_1 (.node(CLK_EN));
  // Switch switch_1: pin names not known; wires that end beside it: switch_1_p1, CLK_EN
  Pull_Resistor #(.pull(1)) pull_resistor_2 (.node(switch_1_p1));
  Pull_Resistor pull_resistor_3 (.node(REGA_OUTPUT));
  // Switch switch_2: pin names not known; wires that end beside it: switch_2_p1, REGA_OUTPUT
  Pull_Resistor #(.pull(1)) pull_resistor_4 (.node(switch_2_p1));
  LED led_1 (.in(CLK_IN));
  Pull_Resistor pull_resistor_5 (.node(CLK_HALT));
  // Switch switch_3: pin names not known; wires that end beside it: switch_3_p1, CLK_HALT
  Pull_Resistor #(.pull(1)) pull_resistor_6 (.node(switch_3_p1));
  Pull_Resistor pull_resistor_7 (.node(REGA_WRITE));
  // Switch switch_4: pin names not known; wires that end beside it: switch_4_p1, REGA_WRITE
  Pull_Resistor #(.pull(1)) pull_resistor_8 (.node(switch_4_p1));
  Pull_Resistor pull_resistor_9 (.node(DBUS));
  assign DBUS = pull_resistor_10_node ? DATA_INPUT_sw1 : 8'bz;  // Controlled_Buffer controlled_buffer_1
  Pull_Resistor pull_resistor_10 (.node(pull_resistor_10_node));
  // Switch switch_5: pin names not known; wires that end beside it: switch_5_p1, pull_resistor_10_node
  Pull_Resistor #(.pull(1)) pull_resistor_11 (.node(switch_5_p1));
  Pull_Resistor pull_resistor_12 (.node(CTR_EN));
  // Switch switch_6: pin names not known; wires that end beside it: switch_6_p1, CTR_EN
  Pull_Resistor #(.pull(1)) pull_resistor_13 (.node(switch_6_p1));
  // LedBar #(.inputtype("row")) ledbar_1: pin names not known; wires that end beside it: DBUS
  DipSwitch DATA_INPUT (
    .sw1(DATA_INPUT_sw1[0]), .sw2(DATA_INPUT_sw1[1]), .sw3(DATA_INPUT_sw1[2]), .sw4(DATA_INPUT_sw1[3]),
    .sw5(DATA_INPUT_sw1[4]), .sw6(DATA_INPUT_sw1[5]), .sw7(DATA_INPUT_sw1[6]), .sw8(DATA_INPUT_sw1[7]));
  Pull_Resistor #(.pull(1)) pull_resistor_14 (.node(pull_resistor_14_node));
  Pull_Resistor pull_resistor_15 (.node(REGB_OUTPUT));
  // Switch switch_7: pin names not known; wires that end beside it: switch_7_p1, REGB_OUTPUT
  Pull_Resistor #(.pull(1)) pull_resistor_16 (.node(switch_7_p1));
  Pull_Resistor pull_resistor_17 (.node(CTR_CLR));
  // Switch switch_8: pin names not known; wires that end beside it: pull_resistor_14_node, CTR_CLR
  // Switch switch_9: pin names not known; wires that end beside it: switch_9_p1, REGB_WRITE
  Pull_Resistor #(.pull(1)) pull_resistor_18 (.node(switch_9_p1));
  Pull_Resistor pull_resistor_19 (.node(CTR_JMP));
  // Switch switch_10: pin names not known; wires that end beside it: switch_10_p1, CTR_JMP
  Pull_Resistor #(.pull(1)) pull_resistor_20 (.node(switch_10_p1));
  Pull_Resistor pull_resistor_21 (.node(REGB_WRITE));
  Pull_Resistor pull_resistor_22 (.node(CTR_OUT));
  // Switch switch_11: pin names not known; wires that end beside it: switch_11_p1, CTR_OUT
  Pull_Resistor #(.pull(1)) pull_resistor_23 (.node(switch_11_p1));
  Button button_2 (.out(REGISTER_CLEAR));
endmodule

module display (
  input  [7:0] in_1
);

  wire d_ff_1_qn, d_ff_2_qn, decoder_1_out0, decoder_1_out1, decoder_1_out2, decoder_1_out3,
       MULTIPLEX_DISP_CLOCK_out;
  wire [1:0] d_ff_1_q;
  wire [7:0] rom_1_data;

  _7_Segment_Display u_7_segment_display_1 (
    .g(rom_1_data[6]), .f(rom_1_data[5]), .a(rom_1_data[0]), .b(rom_1_data[1]), .e(rom_1_data[4]),
    .d(rom_1_data[3]), .c(rom_1_data[2]), .dp(rom_1_data[7]));
  ROM rom_1 (.addr(in_1), .data(rom_1_data));
  D_Flip_Flop d_ff_1 (
    .D(d_ff_1_qn), .clk(MULTIPLEX_DISP_CLOCK_out), .Q(d_ff_1_q[0]), .Qn(d_ff_1_qn));  // open: preset, reset
  Clock MULTIPLEX_DISP_CLOCK (.out(MULTIPLEX_DISP_CLOCK_out));
  D_Flip_Flop d_ff_2 (.D(d_ff_2_qn), .clk(d_ff_1_qn), .Q(d_ff_1_q[1]), .Qn(d_ff_2_qn));  // open: preset, reset
  // LedBar #(.inputtype("row")) ledbar_1: pin names not known; wires that end beside it: rom_1_data
  Decoder #(.select(2)) decoder_1 (
    .out0(decoder_1_out0), .out1(decoder_1_out1), .out2(decoder_1_out2), .out3(decoder_1_out3), .sel(d_ff_1_q));  // open: en
  Controlled_Buffer #(.width(8)) controlled_buffer_1 (.in(rom_1_data), .en(decoder_1_out0));  // open: out
  _7_Segment_Display u_7_segment_display_2 ();  // open: g, f, a, b, e, d, c, dp
  Controlled_Buffer #(.width(8)) controlled_buffer_2 (.in(rom_1_data), .en(decoder_1_out1));  // open: out
  _7_Segment_Display u_7_segment_display_3 ();  // open: g, f, a, b, e, d, c, dp
  Controlled_Buffer #(.width(8)) controlled_buffer_3 (.in(rom_1_data), .en(decoder_1_out2));  // open: out
  Controlled_Buffer #(.width(8)) controlled_buffer_4 (.in(rom_1_data), .en(decoder_1_out3));  // open: out
  _7_Segment_Display u_7_segment_display_4 ();  // open: g, f, a, b, e, d, c, dp
  _7_Segment_Display u_7_segment_display_5 ();  // open: g, f, a, b, e, d, c, dp

  // Notes on the sheet:
  //   contents of rom_1 (hex, n*v repeats v):
  //   3f 6 5b 4f 66 6d 7d 7 7f 6f 0 0 77 7c
endmodule

module gen_register (
  input  WRITE_ENABLE,
  input  OUTPUT_ENABLE,
  input  CLEAR,
  input  CLK,
  output [7:0] DBUS
);

  wire [3:0] LSB_q, MSB_q;

  Register #(.width(4)) LSB (.D(DBUS[3:0]), .en(WRITE_ENABLE), .clk(CLK), .Q(LSB_q), .clr(CLEAR));
  assign DBUS = OUTPUT_ENABLE ? {MSB_q, LSB_q} : 8'bz;  // Controlled_Buffer controlled_buffer_1
  Register #(.width(4)) MSB (.D(DBUS[7:4]), .en(WRITE_ENABLE), .clk(CLK), .Q(MSB_q), .clr(CLEAR));
  // LedBar #(.inputtype("row")) ledbar_1: pin names not known; wires that end beside it: {MSB_q, LSB_q}

  // Notes on the sheet:
  //   output
endmodule

module main_circuit (
);

  wire and_2_out, and_3_out, binary_to_bcd_converter_1_p2, binary_to_bcd_converter_1_p3,
       binary_to_bcd_converter_1_p4, binary_to_bcd_converter_2_p4, binary_to_bcd_converter_3_p2,
       binary_to_bcd_converter_3_p3, binary_to_bcd_converter_3_p4, binary_to_bcd_converter_4_p2,
       binary_to_bcd_converter_4_p3, binary_to_bcd_converter_4_p4, CLK, CLK_EN, CLK_HALT, CLK_PLS, CTR_CLR,
       CTR_EN, CTR_JMP, CTR_OUT, n7_segment_display_4_p1, n7_segment_display_4_p2, n74161_1_pin15,
       n74283_1_pin2, n74283_1_pin6, n74283_1_pin7, n74283_1_pin11, n74283_1_pin15, n74283_2_pin2,
       n74283_2_pin6, n74283_2_pin11, n74283_2_pin15, nor_1_out, nor_2_out, nor_3_out, nor_5_out, nor_6_out,
       nor_7_out, nor_8_out, OSCILLATOR_INPUT_out, pull_resistor_15_node, pull_resistor_32_node, REG_CLR,
       REGA_OUT, REGA_WRITE, REGALU_WRITE, REGALU_ZERO, REGB_OUT, REGB_WRITE, SUM_OUT, SUM_SUB, switch_1_p1,
       switch_2_p1, switch_3_p1, switch_4_p1, switch_5_p1, switch_6_p1, switch_7_p1, switch_8_p1,
       switch_10_p1, switch_11_p1, switch_12_p1, switch_13_p1, switch_14_p1, switch_15_p1;
  wire [3:0] register_1_q, undriven;
  wire [7:0] AREG_BUS, BREG_BUS, DATA_INPUT_sw1, DBUS, n74161_1_pin14, n74283_1_pin4;

  LED led_1 (.in(CLK));
  Button button_1 (.out(CLK_PLS));
  Pull_Resistor pull_resistor_1 (.node(REGALU_WRITE));
  // Switch switch_1: pin names not known; wires that end beside it: switch_1_p1, REGALU_WRITE
  Pull_Resistor #(.pull(1)) pull_resistor_2 (.node(switch_1_p1));
  Pull_Resistor pull_resistor_3 (.node(SUM_OUT));
  // Switch switch_2: pin names not known; wires that end beside it: switch_2_p1, SUM_OUT
  Pull_Resistor #(.pull(1)) pull_resistor_4 (.node(switch_2_p1));
  Pull_Resistor pull_resistor_5 (.node(DBUS));
  assign DBUS = switch_3_p1 ? DATA_INPUT_sw1 : 8'bz;  // Controlled_Buffer controlled_buffer_1
  Pull_Resistor #(.pull(1)) pull_resistor_6 ();  // open: node
  // Switch switch_3: pin names not known; wires that end beside it: switch_3_p1
  Pull_Resistor pull_resistor_7 (.node(CLK_EN));
  // Switch switch_4: pin names not known; wires that end beside it: switch_4_p1, CLK_EN
  Pull_Resistor #(.pull(1)) pull_resistor_8 (.node(switch_4_p1));
  Pull_Resistor pull_resistor_9 (.node(REGA_OUT));
  // Switch switch_5: pin names not known; wires that end beside it: switch_5_p1, REGA_OUT
  Pull_Resistor #(.pull(1)) pull_resistor_10 (.node(switch_5_p1));
  // Switch switch_6: pin names not known; wires that end beside it: switch_6_p1, SUM_SUB
  Pull_Resistor #(.pull(1)) pull_resistor_11 (.node(switch_6_p1));
  Clock OSCILLATOR_INPUT (.out(OSCILLATOR_INPUT_out));
  // LedBar #(.inputtype("row")) ledbar_1: pin names not known; wires that end beside it: DBUS
  Pull_Resistor pull_resistor_12 (.node(switch_3_p1));
  DipSwitch DATA_INPUT (
    .sw1(DATA_INPUT_sw1[0]), .sw2(DATA_INPUT_sw1[1]), .sw3(DATA_INPUT_sw1[2]), .sw4(DATA_INPUT_sw1[3]),
    .sw5(DATA_INPUT_sw1[4]), .sw6(DATA_INPUT_sw1[5]), .sw7(DATA_INPUT_sw1[6]), .sw8(DATA_INPUT_sw1[7]));
  Pull_Resistor pull_resistor_13 (.node(CLK_HALT));
  // Switch switch_7: pin names not known; wires that end beside it: switch_7_p1, CLK_HALT
  Pull_Resistor #(.pull(1)) pull_resistor_14 (.node(switch_7_p1));
  Pull_Resistor #(.pull(1)) pull_resistor_15 (.node(pull_resistor_15_node));
  Pull_Resistor pull_resistor_16 (.node(REGB_OUT));
  // Switch switch_8: pin names not known; wires that end beside it: switch_8_p1, REGB_OUT
  Pull_Resistor #(.pull(1)) pull_resistor_17 (.node(switch_8_p1));
  Pull_Resistor pull_resistor_18 (.node(SUM_SUB));
  Pull_Resistor pull_resistor_19 (.node(REGA_WRITE));
  // Switch switch_9: pin names not known; wires that end beside it: pull_resistor_15_node, REGA_WRITE
  Pull_Resistor pull_resistor_20 (.node(REGB_WRITE));
  // Switch switch_10: pin names not known; wires that end beside it: switch_10_p1, REGB_WRITE
  Pull_Resistor #(.pull(1)) pull_resistor_21 (.node(switch_10_p1));
  Pull_Resistor pull_resistor_22 (.node(CTR_EN));
  // Switch switch_11: pin names not known; wires that end beside it: switch_11_p1, CTR_EN
  Pull_Resistor #(.pull(1)) pull_resistor_23 (.node(switch_11_p1));
  Pull_Resistor pull_resistor_24 (.node(REGB_OUT));
  // Switch switch_12: pin names not known; wires that end beside it: switch_12_p1, REGB_OUT
  Pull_Resistor #(.pull(1)) pull_resistor_25 (.node(switch_12_p1));
  nor nor_1 (nor_1_out, ~OSCILLATOR_INPUT_out, ~CLK_EN);  // NOR_Gate
  nor nor_2 (nor_2_out, ~CLK_PLS, CLK_EN);  // NOR_Gate
  // Binary_to_BCD_converter #(.binvalue(8)) binary_to_bcd_converter_1: pin names not known; wires that end beside it: DBUS, binary_to_bcd_converter_1_p2, binary_to_bcd_converter_1_p3, binary_to_bcd_converter_1_p4
  Pull_Resistor pull_resistor_26 (.node(CTR_CLR));
  // Switch switch_13: pin names not known; wires that end beside it: switch_13_p1, CTR_CLR
  Pull_Resistor #(.pull(1)) pull_resistor_27 (.node(switch_13_p1));
  Button button_2 (.out(REG_CLR));
  nor nor_3 (nor_3_out, nor_1_out, nor_2_out);
  Pull_Resistor pull_resistor_28 (.node(CTR_JMP));
  // Switch switch_14: pin names not known; wires that end beside it: switch_14_p1, CTR_JMP
  Pull_Resistor #(.pull(1)) pull_resistor_29 (.node(switch_14_p1));
  Pull_Resistor pull_resistor_30 (.node(REGB_WRITE));
  // Switch switch_15: pin names not known; wires that end beside it: switch_15_p1, REGB_WRITE
  Pull_Resistor #(.pull(1)) pull_resistor_31 (.node(switch_15_p1));
  Pull_Resistor #(.pull(1)) pull_resistor_32 (.node(pull_resistor_32_node));
  Button button_3 (.out(REG_CLR));
  nor nor_4 (CLK, nor_3_out, CLK_HALT);
  // _7_Segment_Display #(.decimalPoint("false")) 7_segment_display_1: pin names not known; wires that end beside it: binary_to_bcd_converter_1_p2, binary_to_bcd_converter_1_p3
  // BCD_to_7_Segment_decoder bcd_to_7_segment_decoder_1: pin names not known
  Pull_Resistor pull_resistor_33 (.node(CTR_OUT));
  // Switch switch_16: pin names not known; wires that end beside it: pull_resistor_32_node, CTR_OUT
  // _7_Segment_Display #(.decimalPoint("false")) 7_segment_display_2: pin names not known; wires that end beside it: binary_to_bcd_converter_1_p3, binary_to_bcd_converter_1_p4
  _7_Segment_Display #(.decimalPoint("false")) u_7_segment_display_3 ();  // open: g, f, a, b, e, d, c
  // BCD_to_7_Segment_decoder bcd_to_7_segment_decoder_2: pin names not known
  // BCD_to_7_Segment_decoder bcd_to_7_segment_decoder_3: pin names not known
  Register #(.width(4)) register_1 (
    .D(undriven), .en(REGALU_WRITE), .clk(CLK), .Q({register_1_q[3:2], REGALU_ZERO, register_1_q[0]}),
    .clr(REG_CLR));
  and and_1 (undriven[1], and_2_out, and_3_out);
  and and_2 (and_2_out, nor_5_out, nor_6_out);
  and and_3 (and_3_out, nor_7_out, nor_8_out);
  nor nor_5 (nor_5_out, n74283_1_pin4[0], n74283_1_pin4[1]);
  nor nor_6 (nor_6_out, n74283_1_pin4[2], n74283_1_pin4[3]);
  nor nor_7 (nor_7_out, n74283_1_pin4[4], n74283_1_pin4[5]);
  nor nor_8 (nor_8_out, n74283_1_pin4[6], n74283_1_pin4[7]);
  assign DBUS = SUM_OUT ? n74283_1_pin4 : 8'bz;  // Controlled_Buffer controlled_buffer_2
  _74161 u_74161_1 (
    .pin1(CTR_CLR), .pin2(CLK), .pin3(DBUS[0]), .pin4(DBUS[1]), .pin5(DBUS[2]), .pin6(DBUS[3]),
    .pin7(CTR_EN), .pin15(n74161_1_pin15), .pin14(n74161_1_pin14[0]), .pin13(n74161_1_pin14[1]),
    .pin12(n74161_1_pin14[2]), .pin11(n74161_1_pin14[3]), .pin10(CTR_EN), .pin9(CTR_JMP));
  Register #(.width(4)) LSB (.D(DBUS[3:0]), .en(REGA_WRITE), .clk(CLK), .Q(AREG_BUS[3:0]), .clr(REG_CLR));
  Register #(.width(4)) register_2 (.D(DBUS[3:0]), .en(REGB_WRITE), .clk(CLK), .Q(BREG_BUS[3:0]), .clr(REG_CLR));
  _74283 u_74283_1 (
    .pin1(n74283_1_pin4[1]), .pin2(n74283_1_pin2), .pin3(AREG_BUS[2]), .pin4(n74283_1_pin4[0]),
    .pin5(AREG_BUS[3]), .pin6(n74283_1_pin6), .pin7(n74283_1_pin7), .pin15(n74283_1_pin15),
    .pin14(AREG_BUS[0]), .pin13(n74283_1_pin4[2]), .pin12(AREG_BUS[1]), .pin11(n74283_1_pin11),
    .pin10(n74283_1_pin4[3]));  // open: pin9
  // LedBar #(.inputtype("row")) ledbar_2: pin names not known; wires that end beside it: n74283_1_pin4
  assign DBUS = CTR_OUT ? n74161_1_pin14 : 8'bz;  // Controlled_Buffer controlled_buffer_3
  // _7_Segment_Display #(.decimalPoint("false")) 7_segment_display_4: pin names not known; wires that end beside it: n7_segment_display_4_p1, n7_segment_display_4_p2
  // BCD_to_7_Segment_decoder bcd_to_7_segment_decoder_4: pin names not known
  // Binary_to_BCD_converter #(.binvalue(8)) binary_to_bcd_converter_2: pin names not known; wires that end beside it: n74283_1_pin4, n7_segment_display_4_p1, n7_segment_display_4_p2, binary_to_bcd_converter_2_p4
  _74161 u_74161_2 (
    .pin1(CTR_CLR), .pin2(CLK), .pin3(DBUS[4]), .pin4(DBUS[5]), .pin5(DBUS[6]), .pin6(DBUS[7]),
    .pin7(CTR_EN), .pin14(n74161_1_pin14[4]), .pin13(n74161_1_pin14[5]), .pin12(n74161_1_pin14[6]),
    .pin11(n74161_1_pin14[7]), .pin10(n74161_1_pin15), .pin9(CTR_JMP));  // open: pin15
  assign DBUS = REGA_OUT ? AREG_BUS : 8'bz;  // Controlled_Buffer controlled_buffer_4
  Register #(.width(4)) MSB (.D(DBUS[7:4]), .en(REGA_WRITE), .clk(CLK), .Q(AREG_BUS[7:4]), .clr(REG_CLR));
  assign DBUS = REGB_OUT ? BREG_BUS : 8'bz;  // Controlled_Buffer controlled_buffer_5
  Register #(.width(4)) register_3 (.D(DBUS[7:4]), .en(REGB_WRITE), .clk(CLK), .Q(BREG_BUS[7:4]), .clr(REG_CLR));
  // _7_Segment_Display #(.decimalPoint("false")) 7_segment_display_5: pin names not known; wires that end beside it: n7_segment_display_4_p2, binary_to_bcd_converter_2_p4
  _7_Segment_Display #(.decimalPoint("false")) u_7_segment_display_6 ();  // open: g, f, a, b, e, d, c
  // BCD_to_7_Segment_decoder bcd_to_7_segment_decoder_5: pin names not known
  // BCD_to_7_Segment_decoder bcd_to_7_segment_decoder_6: pin names not known
  _74283 u_74283_2 (
    .pin1(n74283_1_pin4[6]), .pin2(n74283_2_pin2), .pin3(AREG_BUS[6]), .pin4(n74283_1_pin4[7]),
    .pin5(AREG_BUS[7]), .pin6(n74283_2_pin6), .pin7(SUM_SUB), .pin15(n74283_2_pin15), .pin14(AREG_BUS[5]),
    .pin13(n74283_1_pin4[5]), .pin12(AREG_BUS[4]), .pin11(n74283_2_pin11), .pin10(n74283_1_pin4[4]),
    .pin9(n74283_1_pin7));
  // LedBar #(.inputtype("row")) ledbar_3: pin names not known; wires that end beside it: n74161_1_pin14
  // LedBar #(.inputtype("row")) ledbar_4: pin names not known; wires that end beside it: AREG_BUS
  // LedBar #(.inputtype("row")) ledbar_5: pin names not known; wires that end beside it: BREG_BUS
  // Binary_to_BCD_converter #(.binvalue(8)) binary_to_bcd_converter_3: pin names not known; wires that end beside it: AREG_BUS, binary_to_bcd_converter_3_p2, binary_to_bcd_converter_3_p3, binary_to_bcd_converter_3_p4
  // Binary_to_BCD_converter #(.binvalue(8)) binary_to_bcd_converter_4: pin names not known; wires that end beside it: BREG_BUS, binary_to_bcd_converter_4_p2, binary_to_bcd_converter_4_p3, binary_to_bcd_converter_4_p4
  // _7_Segment_Display #(.decimalPoint("false")) 7_segment_display_7: pin names not known; wires that end beside it: binary_to_bcd_converter_3_p2, binary_to_bcd_converter_3_p3
  // _7_Segment_Display #(.decimalPoint("false")) 7_segment_display_8: pin names not known; wires that end beside it: binary_to_bcd_converter_3_p3, binary_to_bcd_converter_3_p4
  // BCD_to_7_Segment_decoder bcd_to_7_segment_decoder_7: pin names not known
  // BCD_to_7_Segment_decoder bcd_to_7_segment_decoder_8: pin names not known
  // _7_Segment_Display #(.decimalPoint("false")) 7_segment_display_9: pin names not known; wires that end beside it: binary_to_bcd_converter_4_p2, binary_to_bcd_converter_4_p3
  // BCD_to_7_Segment_decoder bcd_to_7_segment_decoder_9: pin names not known
  _7_Segment_Display #(.decimalPoint("false")) u_7_segment_display_10 ();  // open: g, f, a, b, e, d, c
  // BCD_to_7_Segment_decoder bcd_to_7_segment_decoder_10: pin names not known
  // _7_Segment_Display #(.decimalPoint("false")) 7_segment_display_11: pin names not known; wires that end beside it: binary_to_bcd_converter_4_p3, binary_to_bcd_converter_4_p4
  _7_Segment_Display #(.decimalPoint("false")) u_7_segment_display_12 ();  // open: g, f, a, b, e, d, c
  // BCD_to_7_Segment_decoder bcd_to_7_segment_decoder_11: pin names not known
  // BCD_to_7_Segment_decoder bcd_to_7_segment_decoder_12: pin names not known
  xor xor_1 (n74283_2_pin11, SUM_SUB, BREG_BUS[7]);
  xor xor_2 (n74283_2_pin15, SUM_SUB, BREG_BUS[6]);
  xor xor_3 (n74283_2_pin2, SUM_SUB, BREG_BUS[5]);
  xor xor_4 (n74283_2_pin6, SUM_SUB, BREG_BUS[4]);
  xor xor_5 (n74283_1_pin11, SUM_SUB, BREG_BUS[3]);
  xor xor_6 (n74283_1_pin15, SUM_SUB, BREG_BUS[2]);
  xor xor_7 (n74283_1_pin2, SUM_SUB, BREG_BUS[1]);
  xor xor_8 (n74283_1_pin6, SUM_SUB, BREG_BUS[0]);

  // Notes on the sheet:
  //   Clock Logic
  //   ALU Flag Register
  //   Zero Flag Logic
  //   jump/load line
  //   Program Counter
  //   A Register
  //   A Register
  //   carry line
  //   ALU ADD/SUB
  //   output
  //   inputs
  //   output
  //   output
  //   carry line
  //   Subtraction/Two's Complement Logic
  //   lsb
endmodule
